# Fritzing sketch DeviceWheel-circuit (saved by Fritzing 0.9.3b)

parts:
  Part1 = Adafruit HUZZAH32 ESP32 Feather [part_number="Adafruit #3405"]
  R1 = Resistor [tolerance=±5% resistance=1k package="2010 [SMD]"]
  LED1 = LED - 3mm [color="Blue (430nm)" package="3 mm [THT]"]
  S3 = Toggle Switch [package=THT]
  U1 = Vibration Motor- ROB-08449 [package=vibe-motor-10mm]
  IC2 = DIP - 10 pins [chip_label=IC package="DIP (Dual Inline) [THT]"]

nets:
  N1: Part1.IO21, IC2.INT3
  N2: Part1.IO17, IC2.INT4
  GND: Part1.GND, LED1.cathode, S3.L1, IC2.-
  N3: Part1.3.3V, IC2.+
  N4: Part1.EN, S3.COM
  N5: Part1.IO12_A11, R1.Pin_1
  N6: R1.Pin_0, LED1.anode
  N7: U1.+, IC2.MOTOR-B#6
  N8: U1.-, IC2.MOTOR-B#5

custom parts:
  DIP - 10 pins: A DIP stand-in part for whatever IC you want. With 10 pins on a 300mil dual inline package (DIP) footprint.
