# Fritzing sketch SignalStrength-circuit (saved by Fritzing 0.9.3b)

parts:
  Part1 = Adafruit HUZZAH32 ESP32 Feather [part_number="Adafruit #3405"]
  Voltmeter2 = Voltmeter
  R1 = Resistor [tolerance=±5% resistance=1k package="2010 [SMD]"]
  LED1 = LED - 3mm [color="Blue (430nm)" package="3 mm [THT]"]
  S3 = Toggle Switch [package=THT]

nets:
  N1: Part1.IO17, Voltmeter2.Positive
  GND: Part1.GND, Voltmeter2.Com, LED1.cathode, S3.L1
  N2: Part1.EN, S3.COM
  N3: Part1.IO12_A11, R1.Pin_1
  N4: R1.Pin_0, LED1.anode

custom parts:
  Voltmeter: A Standard Multimeter in Current mode
