# Fritzing sketch SignalStrength (saved by Fritzing 0.9.3b)

parts:
  Part1 = Adafruit HUZZAH32 ESP32 Feather [part_number="Adafruit #3405"]
  R1 = Resistor [tolerance=±5% resistance=1k package="2010 [SMD]"]
  LED1 = smd LED [color="Blue (430nm)" package="0603 [SMD]"]
  S2 = SPST Switch [package=switch-spdt]  # not connected
  Voltmeter1 = Voltmeter

nets:
  N1: Part1.IO17, Voltmeter1.Positive
  GND: Part1.GND, LED1.cathode, Voltmeter1.Com
  N2: Part1.IO12_A11, R1.Pin_0
  N3: R1.Pin_1, LED1.anode

custom parts:
  Voltmeter: A Standard Multimeter in Current mode
