# Fritzing sketch TrafficMonitor-circuit (saved by Fritzing 0.9.3b)

parts:
  WeMos_D1_Mini1 = WeMos D1 Mini
  MCU1 = Raspberry Pi Zero
  R2 = Resistor [tolerance=±5% resistance=1k package="2010 [SMD]"]
  LED2 = LED - 3mm [color="Blue (430nm)" package="3 mm [THT]"]

nets:
  N1: WeMos_D1_Mini1.3V3, MCU1.pin_1, MCU1.pin_17
  N2: WeMos_D1_Mini1.D1, R2.Pin_1
  GND: WeMos_D1_Mini1.G, MCU1.pin_6, MCU1.pin_9, MCU1.pin_14, MCU1.pin_30, LED2.cathode
  N3: WeMos_D1_Mini1.RX, MCU1.pin_8
  N4: WeMos_D1_Mini1.TX, MCU1.pin_10
  N5: R2.Pin_0, LED2.anode
